# Fritzing sketch omni_rover_L9110S (saved by Fritzing 0.9.3b)

parts:
  Raspberry_Pi_Zero1 = Raspberry Pi Zero
  U2 = L9110 H-bridge module [part_number="L9110 H-bridge"]
  U3 = L9110 H-bridge module [part_number="L9110 H-bridge"]
  M3 = DC Motor
  M4 = DC Motor
  M5 = DC Motor
  M6 = DC Motor
  VCC2 = 4 x AAA Battery Mount

nets:
  GND: Raspberry_Pi_Zero1.GPIO6, Raspberry_Pi_Zero1.GND, U2.GND, U3.GND, U3.A-IB
  N1: Raspberry_Pi_Zero1.GPIO13, U3.B-IA
  N2: Raspberry_Pi_Zero1.GPIO19, U3.B-IB
  N3: Raspberry_Pi_Zero1.GPIO26, U3.A-IA
  N4: Raspberry_Pi_Zero1.GPIO21, U2.A-IB
  N5: Raspberry_Pi_Zero1.GPIO20, U2.A-IA
  N6: Raspberry_Pi_Zero1.GPIO16, U2.B-IB
  N7: Raspberry_Pi_Zero1.GPIO12, U2.B-IA
  VCC: U2.VCC, U3.VCC, VCC2.+
  N8: U2.MOTOR_A-A, M3.pin_2
  N9: U2.MOTOR_A-B, M3.pin_1
  N10: U2.MOTOR_B-A, M4.pin_2
  N11: U2.MOTOR_B-B, M4.pin_1
  N12: U3.MOTOR_A-A, M6.pin_2
  N13: U3.MOTOR_A-B, M6.pin_1
  N14: U3.MOTOR_B-A, M5.pin_2
  N15: U3.MOTOR_B-B, M5.pin_1
